# Fritzing sketch fritzing file (saved by Fritzing 0.9.3b)
breadboards: 1

parts:
  Part2 = Arduino Uno (Rev3)
  Part1 = Soil Moisture Sensor
  K1 = Relay [part_number=FRS1B-S package=THT]
  M1 = DC Motor  # not connected

nets:
  N1: Part2.D11_PWM/MOSI, K1.COIL2
  N2: Part2.D12/MISO, Part1.SIG
  5V: Part2.5V, Part1.VCC
  GND: Part2.GND, Part1.GND, K1.COIL1

notes:
  Dc motor pump
  DC POWER SUPPLY
  DC 7~12V

// code stored in the sketch: Automatic_plant_watering.ino
#define soil_moisture 12
#define pump 11

void setup() {
 
  pinMode(pump, OUTPUT);
  pinMode(soil_moisture, INPUT);
  Serial.begin(9600);
}

void loop() {
 
  int val = digitalRead(soil_moisture);
  Serial.println(val);
  if(val == 1)
  {
    digitalWrite(pump, HIGH);
  }
  else
  {
    digitalWrite(pump, LOW);
  }
}
